# Fritzing sketch Master & Salve schematic (saved by Fritzing 0.9.3b)

parts:
  Part1 = Bluetooth HC-05 Macho
  Part3 = Arduino Uno (Rev3)
  Part4 = Arduino Uno (Rev3)
  Part5 = Bluetooth HC-05 Macho
  S1 = Pushbutton [package="[THT]"]
  S2 = Pushbutton [package="[THT]"]
  LED2 = LED - 5mm [color="Red (633nm)" package="5 mm [THT]"]
  R1 = Resistor [tolerance=±5% resistance=220 package="0603 [SMD]"]
  R2 = Resistor [tolerance=±5% resistance=220 package="0603 [SMD]"]
  R3 = Resistor [tolerance=±5% resistance=220 package="0603 [SMD]"]
  R4 = Resistor [tolerance=±5% resistance=220 package="0603 [SMD]"]
  R5 = Resistor [tolerance=±5% resistance=220 package="0603 [SMD]"]  # not connected
  LED3 = LED - 5mm [color="Red (633nm)" package="5 mm [THT]"]
  R6 = Resistor [tolerance=±5% resistance=220 package="0603 [SMD]"]  # not connected
  R7 = Resistor [tolerance=±5% resistance=220 package=THT]

nets:
  N1: Part1.TXD, R2.Pin_1
  N2: Part1.RXD, Part3.D0/RX
  VCC: Part1.VCC, Part3.5V
  GND: Part1.GND, Part3.GND, LED3.cathode
  N3: Part3.D8, LED3.anode
  N4: Part3.D1/TX, R2.Pin_0
  N5: Part3.D7, S2.Pin_3, S2.Pin_4, R7.Pin_1
  N6: Part4.D8, LED2.anode
  N7: Part4.D0/RX, Part5.TXD
  N8: Part4.D1/TX, R4.Pin_0
  N9: Part4.D7, S1.Pin_3
  5V: Part4.5V, Part5.VCC, S1.Pin_1, S1.Pin_2
  GND_2: Part4.GND, Part5.GND, LED2.cathode, R1.Pin_0, R3.Pin_0
  N10: Part5.RXD, R3.Pin_1, R4.Pin_1

notes:
  2K
  1K
  Slave
  10K
  Master
